# Fritzing sketch doordrop-pcb-wiring (saved by Fritzing 1.0.2b)
circuit board: 8.46667cm x 5.64444cm
breadboards: 1

parts:
  2n2222 = TRANSISTOR_NPN [package=to-92-ammo]
  R1 = Resistor [tolerance=±5% resistance=1k package="2010 [SMD]"]
  PIR1 = PIR sensor
  GM1 = GM67 Barcode Reader
  U1 = NodeMCU V3.0
  LCD = LCD1602-I2C
  Part1 = ws2812b [package="smd 2812b"]
  DC1 = DC_DC_XL4016 [package=board_screw]

nets:
  GND: 2n2222.E, PIR1.GND, U1.GND#6, U1.GND#13, U1.GND#16, U1.GND#33, Part1.VSS, DC1.OUT-
  N1: 2n2222.B, R1.Pin_0
  N2: 2n2222.C, GM1.GND
  N3: R1.Pin_1, U1.D7
  VDD: PIR1.VDD, GM1.5V, U1.VU, LCD.VCC
  N4: PIR1.SIG, U1.D6
  N5: GM1.RX, U1.D3
  N6: GM1.TX, U1.D4
  N7: U1.D1, LCD.SCL
  N8: U1.D2, LCD.SDA
  N9: U1.D5, Part1.DIN
  VIN: U1.Vin, Part1.VDD, DC1.OUT+
  N10: U1.GND#41, LCD.GND

custom parts:
  GM67 Barcode Reader: Header 8 GM67 Barcode Reader V1.0. Please ignore the PCB view of this circuit it does not matter. Please feel free to make this better
  NodeMCU V3.0: ESP8266 based NodeMCU
  LCD1602-I2C: A standard character display, usually with 2x16 characters. Comes in many colors with LCM1602 IIC attached.
